// Logisim project DOMACI2_KOMBINACIONE_NILI.circ as structural Verilog: 2 circuits, main circuit kompleksnoNILI
module kompleksnoNILI (
  input  x1,
  input  x2,
  input  x3,
  input  x4,
  input  x5,
  output y
);

  wire nor_1_out, nor_2_out, nor_3_out, nor_4_out, nor_5_out, nor_6_out, nor_7_out, nor_8_out, nor_9_out,
       nor_10_out, nor_11_out, nor_12_out, nor_13_out, nor_14_out, nor_15_out;

  nor nor_1 (nor_1_out, x1, x1);
  nor nor_2 (nor_2_out, x2, x2);
  nor nor_3 (nor_3_out, x3, x3);
  nor nor_4 (nor_4_out, x4, x4);
  nor nor_5 (nor_5_out, nor_1_out, nor_1_out);
  nor nor_6 (nor_6_out, nor_3_out, nor_3_out);
  nor nor_7 (nor_7_out, nor_4_out, nor_4_out);
  nor nor_8 (nor_8_out, nor_5_out, nor_2_out);
  nor nor_9 (nor_9_out, nor_6_out, nor_7_out);
  nor nor_10 (nor_10_out, nor_8_out, nor_8_out);
  nor nor_11 (nor_11_out, nor_9_out, nor_9_out);
  nor nor_12 (nor_12_out, x5, x5);
  nor nor_13 (nor_13_out, nor_10_out, nor_11_out);
  nor nor_14 (nor_14_out, nor_12_out, nor_12_out);
  nor nor_15 (nor_15_out, nor_13_out, nor_13_out);
  nor nor_16 (y, nor_15_out, nor_14_out);

  // Notes on the sheet:
  //   MOJ DATUM RODJENJA JE 25.10
  //   OVO JE KOMPLEKSNO KOLO
endmodule

module uprosceno (
  input  x1,
  input  x2,
  input  x3,
  input  x4,
  input  x5,
  output y
);

  wire nor_1_out, nor_2_out, nor_3_out, nor_4_out, nor_5_out, nor_6_out, nor_7_out;

  nor nor_1 (nor_1_out, x2, x2);
  nor nor_2 (nor_2_out, x1, nor_1_out);
  nor nor_3 (nor_3_out, x3, x4);
  nor nor_4 (nor_4_out, nor_2_out, nor_2_out);
  nor nor_5 (nor_5_out, nor_3_out, nor_3_out);
  nor nor_6 (nor_6_out, nor_4_out, nor_5_out);
  nor nor_7 (nor_7_out, nor_6_out, nor_6_out);
  nor nor_8 (y, nor_7_out, x5);
endmodule
