// Logisim project Example_1.circ as structural Verilog
module drugo_logicko_kolo (
  input  x1,
  input  x2,
  output y
);

  wire not_1_out, or_1_out;

  or or_1 (or_1_out, x2, x1);
  not not_1 (not_1_out, x1);
  // Probe on or_1_out
  nand nand_1 (y, or_1_out, not_1_out);
  // Probe on y
endmodule
