// Logisim project Example_2.circ as structural Verilog: 1 circuit, main circuit logicko kolo
module logicko_kolo (
  input  x1,
  input  x2,
  output y
);

  wire and_1_out, and_2_out, not_1_out, not_2_out, or_1_out;

  not not_1 (not_1_out, x2);
  not not_2 (not_2_out, x1);
  // Probe on and_1_out
  and and_1 (and_1_out, x2, not_1_out);
  // Probe on and_2_out
  and and_2 (and_2_out, x1, not_2_out);
  // Probe on or_1_out
  or or_1 (or_1_out, and_1_out, and_2_out);
  not not_3 (y, or_1_out);
endmodule
