// Logisim project Example_5.circ as structural Verilog: 2 circuits, main circuit kolo1
module kolo1 (
  input  x1,
  input  x2,
  input  x3,
  input  x4,
  output f
);

  wire and_1_out, not_1_out, not_2_out, not_3_out, or_1_out, or_2_out;

  not not_1 (not_1_out, x3);
  not not_2 (not_2_out, x4);
  or or_1 (or_1_out, x2, not_1_out);
  not not_3 (not_3_out, x1);
  and and_1 (and_1_out, not_2_out, or_1_out);
  or or_2 (or_2_out, not_3_out, x2);
  and and_2 (f, and_1_out, or_2_out);
endmodule

module kolo2 (
  input  x1,
  input  x2,
  input  x3,
  input  x4,
  output out_5
);

  wire nand_1_out, nand_2_out, nand_3_out, nand_4_out, nand_5_out, nand_6_out;

  nand nand_1 (nand_1_out, x2, x2);
  nand nand_2 (nand_2_out, x2, x2);
  nand nand_3 (nand_3_out, x4, x4);
  nand nand_4 (nand_4_out, nand_1_out, x3);
  nand nand_5 (nand_5_out, x1, nand_2_out);
  nand nand_6 (nand_6_out, nand_3_out, nand_4_out, nand_5_out);
  nand nand_7 (out_5, nand_6_out, nand_6_out);
endmodule
