// Logisim project Example_6.circ as structural Verilog: 8 circuits, main circuit kolo1
module kolo1 (
  input  x1,
  input  x2,
  output y
);

  wire not_1_out, not_2_out, or_1_out, or_2_out;

  not not_1 (not_1_out, x2);
  not not_2 (not_2_out, x1);
  // Probe on nothing
  // Probe on nothing
  or or_1 (or_1_out, x1, not_1_out);
  or or_2 (or_2_out, not_2_out, x2);
  // Probe on nothing
  // Probe on nothing
  and and_1 (y, or_1_out, or_2_out);
endmodule

module kolo2 (
  input  x1,
  input  x2,
  output y
);

  wire not_1_out, not_2_out, or_1_out, or_2_out;

  not not_1 (not_1_out, x2);
  not not_2 (not_2_out, x1);
  or or_1 (or_1_out, x1, not_1_out);
  or or_2 (or_2_out, not_2_out, x2);
  and and_1 (y, or_1_out, or_2_out);
endmodule

module kolo3 (
  input  x1,
  input  x2,
  output y
);

  wire nand_1_out, nand_2_out, nand_3_out, nand_4_out, nand_5_out;

  nand nand_1 (nand_1_out, x1, x1);
  nand nand_2 (nand_2_out, x2, x2);
  nand nand_3 (nand_3_out, nand_1_out, x2);
  nand nand_4 (nand_4_out, x1, nand_2_out);
  nand nand_5 (nand_5_out, nand_3_out, nand_4_out);
  nand nand_6 (y, nand_5_out, nand_5_out);
endmodule

module kolo4 (
  input  x1,
  input  x2,
  input  x3,
  input  x4,
  output y
);

  wire kolo3_1_y, kolo3_2_y;

  kolo3 kolo3_1 (.x1(x1), .x2(x2), .y(kolo3_1_y));
  kolo3 kolo3_2 (.x1(x4), .x2(x3), .y(kolo3_2_y));
  kolo3 kolo3_3 (.x1(kolo3_1_y), .x2(kolo3_2_y), .y(y));
endmodule

module kolo5 (
  input  x1,
  input  x2,
  input  x3,
  input  x4,
  output y
);

  wire and_1_out, and_2_out, and_3_out, and_4_out, and_5_out, and_6_out, and_7_out, and_8_out, and_9_out,
       and_10_out, and_11_out, and_12_out, and_13_out, and_14_out, and_15_out, and_16_out, and_17_out,
       and_18_out, and_19_out, and_20_out, and_21_out, and_22_out, and_23_out, and_24_out, not_1_out,
       not_2_out, not_3_out, not_4_out, not_5_out, not_6_out, not_7_out, not_8_out, not_9_out, not_10_out,
       not_11_out, not_12_out, not_13_out, not_14_out, not_15_out, not_16_out, or_1_out, or_2_out, or_3_out,
       or_4_out, or_5_out, or_6_out;

  not not_1 (not_1_out, x1);
  and and_1 (and_1_out, not_1_out, not_2_out);
  not not_2 (not_2_out, x2);
  not not_3 (not_3_out, x3);
  and and_2 (and_2_out, not_3_out, not_4_out);
  not not_4 (not_4_out, x4);
  not not_5 (not_5_out, x1);
  and and_3 (and_3_out, not_5_out, not_6_out);
  not not_6 (not_6_out, x2);
  and and_4 (and_4_out, x3, x4);
  not not_7 (not_7_out, x1);
  and and_5 (and_5_out, not_7_out, x2);
  not not_8 (not_8_out, x3);
  and and_6 (and_6_out, not_8_out, x4);
  not not_9 (not_9_out, x1);
  and and_7 (and_7_out, not_9_out, x2);
  and and_8 (and_8_out, x3, not_10_out);
  not not_10 (not_10_out, x4);
  and and_9 (and_9_out, x1, not_11_out);
  not not_11 (not_11_out, x2);
  not not_12 (not_12_out, x3);
  and and_10 (and_10_out, not_12_out, x4);
  and and_11 (and_11_out, x1, not_13_out);
  not not_13 (not_13_out, x2);
  and and_12 (and_12_out, x3, not_14_out);
  not not_14 (not_14_out, x4);
  and and_13 (and_13_out, x1, x2);
  not not_15 (not_15_out, x3);
  and and_14 (and_14_out, not_15_out, not_16_out);
  not not_16 (not_16_out, x4);
  and and_15 (and_15_out, x1, x2);
  and and_16 (and_16_out, x3, x4);
  and and_17 (and_17_out, and_1_out, and_2_out);
  and and_18 (and_18_out, and_3_out, and_4_out);
  and and_19 (and_19_out, and_5_out, and_6_out);
  and and_20 (and_20_out, and_7_out, and_8_out);
  and and_21 (and_21_out, and_9_out, and_10_out);
  and and_22 (and_22_out, and_11_out, and_12_out);
  and and_23 (and_23_out, and_13_out, and_14_out);
  and and_24 (and_24_out, and_15_out, and_16_out);
  or or_1 (or_1_out, and_17_out, and_18_out);
  or or_2 (or_2_out, and_19_out, and_20_out);
  or or_3 (or_3_out, and_21_out, and_22_out);
  or or_4 (or_4_out, and_23_out, and_24_out);
  or or_5 (or_5_out, or_1_out, or_2_out);
  or or_6 (or_6_out, or_3_out, or_4_out);
  or or_7 (y, or_5_out, or_6_out);
endmodule

module kolo6 (
  input  x1,
  input  x2,
  input  x3,
  input  x4,
  output y
);

  wire nand_1_out, nand_2_out, nand_3_out, nand_4_out, nand_5_out, nand_6_out, nand_7_out, nand_8_out,
       nand_9_out, nand_10_out, nand_11_out, nand_12_out, nand_13_out, nand_14_out, nand_15_out, nand_16_out,
       nand_17_out, nand_18_out, nand_19_out, nand_20_out, nand_21_out, nand_22_out, nand_23_out, nand_24_out;

  nand nand_1 (nand_1_out, x1, x1);
  nand nand_2 (nand_2_out, x2, x2);
  nand nand_3 (nand_3_out, x3, x3);
  nand nand_4 (nand_4_out, x4, x4);
  nand nand_5 (nand_5_out, x1, x1);
  nand nand_6 (nand_6_out, x2, x2);
  nand nand_7 (nand_7_out, x1, x1);
  nand nand_8 (nand_8_out, x3, x3);
  nand nand_9 (nand_9_out, x1, x1);
  nand nand_10 (nand_10_out, x4, x4);
  nand nand_11 (nand_11_out, x2, x2);
  nand nand_12 (nand_12_out, x3, x3);
  nand nand_13 (nand_13_out, x2, x2);
  nand nand_14 (nand_14_out, x4, x4);
  nand nand_15 (nand_15_out, x3, x3);
  nand nand_16 (nand_16_out, x4, x4);
  nand nand_17 (nand_17_out, nand_1_out, nand_2_out, nand_3_out, nand_4_out);
  nand nand_18 (nand_18_out, nand_5_out, nand_6_out, x3, x4);
  nand nand_19 (nand_19_out, nand_7_out, x2, nand_8_out, x4);
  nand nand_20 (nand_20_out, nand_9_out, x2, x3, nand_10_out);
  nand nand_21 (nand_21_out, x1, nand_11_out, nand_12_out, x4);
  nand nand_22 (nand_22_out, x1, nand_13_out, x3, nand_14_out);
  nand nand_23 (nand_23_out, x1, x2, nand_15_out, nand_16_out);
  nand nand_24 (nand_24_out, x1, x2, x3, x4);
  nand nand_25 (y, nand_17_out, nand_18_out, nand_19_out, nand_20_out, nand_21_out, nand_22_out, nand_23_out, nand_24_out);
endmodule

module kolo7 (
  input  x1,
  input  x2,
  input  x3,
  output y
);

  wire and_1_out, and_2_out, not_1_out, not_2_out;

  not not_1 (not_1_out, x3);
  not not_2 (not_2_out, x2);
  and and_1 (and_1_out, x2, not_1_out);
  and and_2 (and_2_out, not_2_out, x1);
  or or_1 (y, and_1_out, and_2_out);
endmodule

module kolo8 (
  input  x1,
  input  x2,
  input  x3,
  input  x4,
  input  x5,
  output y
);

  wire and_1_out, and_2_out, not_1_out, not_2_out;

  not not_1 (not_1_out, x3);
  not not_2 (not_2_out, x2);
  and and_1 (and_1_out, x2, not_1_out);
  and and_2 (and_2_out, not_2_out, x1);
  or or_1 (y, and_1_out, and_2_out);
endmodule
