// Logisim project Example_8.circ as structural Verilog: 2 circuits, main circuit main
module main (
  input  A,
  input  B,
  input  C,
  output a_2,
  output b_2,
  output c_2,
  output d,
  output x,
  output f,
  output g
);

  wire and_1_out, and_2_out, and_3_out, and_4_out, and_5_out, and_6_out, and_7_out, and_8_out, and_9_out,
       and_10_out, and_11_out, and_12_out, and_13_out, and_14_out, and_15_out, and_16_out, and_17_out,
       not_1_out, not_2_out, not_3_out, not_4_out, not_5_out, not_6_out, not_7_out, not_8_out, not_9_out,
       not_10_out, not_11_out, not_12_out, not_13_out, not_14_out, not_15_out, not_16_out, not_17_out,
       not_18_out, not_19_out, not_20_out, not_21_out, or_1_out, or_2_out, or_3_out, or_6_out, or_7_out,
       or_10_out, or_11_out;

  not not_1 (not_1_out, A);
  not not_2 (not_2_out, C);
  not not_3 (not_3_out, B);
  not not_4 (not_4_out, C);
  not not_5 (not_5_out, B);
  not not_6 (not_6_out, B);
  not not_7 (not_7_out, A);
  not not_8 (not_8_out, C);
  not not_9 (not_9_out, C);
  not not_10 (not_10_out, C);
  not not_11 (not_11_out, B);
  not not_12 (not_12_out, C);
  not not_13 (not_13_out, A);
  and and_1 (and_1_out, not_1_out, not_2_out);
  not not_14 (not_14_out, A);
  and and_2 (and_2_out, not_3_out, not_4_out);
  or or_1 (or_1_out, not_5_out, A);
  not not_15 (not_15_out, A);
  not not_16 (not_16_out, C);
  not not_17 (not_17_out, C);
  not not_18 (not_18_out, A);
  and and_3 (and_3_out, A, not_6_out);
  and and_4 (and_4_out, not_7_out, not_8_out);
  and and_5 (and_5_out, B, not_9_out);
  and and_6 (and_6_out, A, not_10_out);
  and and_7 (and_7_out, A, not_11_out);
  not not_19 (not_19_out, B);
  not not_20 (not_20_out, C);
  and and_8 (and_8_out, A, not_12_out);
  and and_9 (and_9_out, not_13_out, B);
  not not_21 (not_21_out, B);
  or or_2 (or_2_out, B, and_1_out);
  and and_10 (and_10_out, A, C);
  or or_3 (or_3_out, not_14_out, and_2_out);
  and and_11 (and_11_out, B, C);
  or or_4 (c_2, or_1_out, C);
  and and_12 (and_12_out, not_15_out, not_16_out);
  and and_13 (and_13_out, B, not_17_out);
  and and_14 (and_14_out, not_18_out, B);
  and and_15 (and_15_out, and_3_out, C);
  or or_5 (x, and_4_out, and_5_out);
  or or_6 (or_6_out, and_6_out, and_7_out);
  and and_16 (and_16_out, not_19_out, not_20_out);
  or or_7 (or_7_out, and_8_out, and_9_out);
  and and_17 (and_17_out, A, not_21_out);
  or or_8 (a_2, or_2_out, and_10_out);
  or or_9 (b_2, or_3_out, and_11_out);
  or or_10 (or_10_out, and_12_out, and_13_out);
  or or_11 (or_11_out, and_14_out, and_15_out);
  or or_12 (f, or_6_out, and_16_out);
  or or_13 (g, or_7_out, and_17_out);
  or or_14 (d, or_10_out, or_11_out);
  _7_Segment_Display u_7_segment_display_1 (.g(g), .f(f), .a(a_2), .b(b_2), .e(x), .d(d), .c(c_2));  // open: dp
endmodule

module alarm (
  input  AD,
  input  AP,
  input  AV,
  output P,
  output V,
  output SR,
  output Z
);

  wire and_1_out, not_1_out, not_2_out;

  not not_1 (not_1_out, AP);
  and and_1 (and_1_out, AD, not_1_out);
  not not_2 (not_2_out, AV);
  and and_2 (SR, and_1_out, not_2_out);

  assign P = AP;
  assign V = AV;
  assign Z = AD;
endmodule
