// Logisim project Primer3.circ as structural Verilog: 1 circuit, main circuit kolo1
module kolo1 (
  input  x1,
  input  x2,
  input  x3,
  input  x4,
  output f
);

  wire and_1_out, and_2_out, and_3_out, not_1_out, not_2_out, not_3_out, not_4_out, not_5_out, not_6_out;

  not not_1 (not_1_out, x3);
  not not_2 (not_2_out, x4);
  not not_3 (not_3_out, x4);
  not not_4 (not_4_out, x1);
  not not_5 (not_5_out, x3);
  not not_6 (not_6_out, x4);
  and and_1 (and_1_out, x1, x2, not_1_out, not_2_out);
  and and_2 (and_2_out, x2, x3, not_3_out);
  and and_3 (and_3_out, not_4_out, x2, not_5_out, not_6_out);
  or or_1 (f, and_1_out, and_2_out, and_3_out);
endmodule
