// Logisim project Primer4.circ as structural Verilog: 2 circuits, main circuit kolo1
module kolo1 (
  input  x1,
  input  x2,
  input  x3,
  input  x4,
  output out_5
);

  wire and_1_out, and_2_out, and_3_out, not_1_out, not_2_out, not_3_out, not_4_out;

  not not_1 (not_1_out, x1);
  not not_2 (not_2_out, x3);
  and and_1 (and_1_out, not_1_out, not_2_out);
  not not_3 (not_3_out, x4);
  not not_4 (not_4_out, x4);
  and and_2 (and_2_out, and_1_out, not_3_out);
  and and_3 (and_3_out, x2, not_4_out);
  or or_1 (out_5, and_2_out, and_3_out);
endmodule

module kolo2 (
  input  x1,
  input  x2,
  input  x3,
  input  x4,
  output f
);

  wire and_1_out, and_2_out, and_3_out, and_4_out, and_5_out, and_6_out, and_7_out, not_1_out, not_2_out,
       not_3_out, not_4_out, not_5_out, not_6_out;

  and and_1 (and_1_out, x1, x1);
  and and_2 (and_2_out, x3, x3);
  and and_3 (and_3_out, x4, x4);
  and and_4 (and_4_out, x4, x4);
  not not_1 (not_1_out, and_1_out);
  not not_2 (not_2_out, and_2_out);
  not not_3 (not_3_out, and_3_out);
  not not_4 (not_4_out, and_4_out);
  and and_5 (and_5_out, not_1_out, not_2_out, not_3_out);
  and and_6 (and_6_out, x2, not_4_out);
  not not_5 (not_5_out, and_5_out);
  not not_6 (not_6_out, and_6_out);
  and and_7 (and_7_out, not_5_out, not_6_out);
  not not_7 (f, and_7_out);
endmodule
