// Logisim project v1.circ as structural Verilog: 3 circuits, main circuit kolo1
module kolo1 (
  input  x1,
  input  x2,
  input  x3,
  input  x4,
  output f
);

  wire and_1_out, and_2_out, and_3_out, not_1_out, not_2_out, not_3_out, not_4_out, not_5_out, not_6_out;

  not not_1 (not_1_out, x3);
  not not_2 (not_2_out, x4);
  not not_3 (not_3_out, x4);
  not not_4 (not_4_out, x1);
  not not_5 (not_5_out, x3);
  not not_6 (not_6_out, x4);
  and and_1 (and_1_out, x1, x2, not_1_out, not_2_out);
  and and_2 (and_2_out, x2, x3, not_3_out);
  and and_3 (and_3_out, not_4_out, x2, not_5_out, not_6_out);
  or or_1 (f, and_1_out, and_2_out, and_3_out);
endmodule

module kolo2 (
  input  x1,
  input  x2,
  input  x3,
  input  x4,
  output f
);

  wire and_1_out, and_2_out, and_3_out, and_4_out, and_5_out, and_6_out, and_7_out, and_8_out, not_1_out,
       not_2_out, not_3_out, not_4_out, not_5_out, not_6_out, or_1_out;

  and and_1 (and_1_out, x1, x2);
  not not_1 (not_1_out, x3);
  and and_2 (and_2_out, not_1_out, not_2_out);
  not not_2 (not_2_out, x4);
  and and_3 (and_3_out, x2, x3);
  not not_3 (not_3_out, x4);
  not not_4 (not_4_out, x1);
  not not_5 (not_5_out, x3);
  not not_6 (not_6_out, x4);
  and and_4 (and_4_out, and_1_out, and_2_out);
  and and_5 (and_5_out, and_3_out, not_3_out);
  and and_6 (and_6_out, not_4_out, x2);
  and and_7 (and_7_out, not_5_out, not_6_out);
  or or_1 (or_1_out, and_4_out, and_5_out);
  and and_8 (and_8_out, and_6_out, and_7_out);
  or or_2 (f, or_1_out, and_8_out);
endmodule

module kolo3 (
  input  x1,
  input  x2,
  input  x3,
  input  x4,
  output f
);

  wire nand_1_out, nand_2_out, nand_3_out, nand_4_out, nand_5_out, nand_6_out, nand_7_out, nand_8_out,
       nand_9_out;

  nand nand_1 (nand_1_out, x3, x3);
  nand nand_2 (nand_2_out, x4, x4);
  nand nand_3 (nand_3_out, x4, x4);
  nand nand_4 (nand_4_out, x1, x1);
  nand nand_5 (nand_5_out, x3, x3);
  nand nand_6 (nand_6_out, x4, x4);
  nand nand_7 (nand_7_out, x1, x2, nand_1_out, nand_2_out);
  nand nand_8 (nand_8_out, x2, x3, nand_3_out);
  nand nand_9 (nand_9_out, nand_4_out, x2, nand_5_out, nand_6_out);
  nand nand_10 (f, nand_7_out, nand_8_out, nand_9_out);
endmodule
