// Logisim project v3.circ as structural Verilog: 4 circuits, main circuit kolo1
module kolo1 (
  input  x1,
  input  x2,
  output f
);

  wire not_1_out, not_2_out, or_1_out, or_2_out;

  not not_1 (not_1_out, x2);
  not not_2 (not_2_out, x1);
  or or_1 (or_1_out, x1, not_1_out);
  or or_2 (or_2_out, not_2_out, x2);
  and and_1 (f, or_1_out, or_2_out);
endmodule

module kolo2 (
  input  x1,
  input  x2,
  output f
);

  wire and_1_out, and_2_out, not_1_out, not_2_out;

  not not_1 (not_1_out, x1);
  not not_2 (not_2_out, x2);
  and and_1 (and_1_out, not_1_out, not_2_out);
  and and_2 (and_2_out, x1, x2);
  or or_1 (f, and_1_out, and_2_out);
endmodule

module kolo3 (
  input  x1,
  input  x2,
  output f
);

  wire nand_1_out, nand_2_out, nand_3_out, nand_4_out, nand_5_out;

  nand nand_1 (nand_1_out, x1, x1);
  nand nand_2 (nand_2_out, x2, x2);
  nand nand_3 (nand_3_out, nand_1_out, x2);
  nand nand_4 (nand_4_out, x1, nand_2_out);
  nand nand_5 (nand_5_out, nand_3_out, nand_4_out);
  nand nand_6 (f, nand_5_out, nand_5_out);
endmodule

module kolo4 (
  input  x1,
  input  x2,
  input  x3,
  input  x4,
  output y
);

  wire kolo1_1_f, kolo1_2_f;

  kolo1 kolo1_1 (.x1(x1), .x2(x2), .f(kolo1_1_f));
  kolo1 kolo1_2 (.x1(x3), .x2(x4), .f(kolo1_2_f));
  kolo1 kolo1_3 (.x1(kolo1_2_f), .x2(kolo1_1_f), .f(y));
endmodule
