// Logisim project v4.circ as structural Verilog: 1 circuit, main circuit kolo1
module kolo1 (
  input  x1,
  input  x2,
  input  x3,
  output out_4,
  output out_5,
  output out_6,
  output out_7,
  output out_8,
  output out_9,
  output out_10,
  output out_11
);

  Decoder #(.select(3)) decoder_1 (
    .out0(out_4), .out1(out_5), .out2(out_6), .out3(out_7), .out4(out_8), .out5(out_9), .out6(out_10),
    .out7(out_11), .sel({x3, x2, x1}), .en(1'b1));
endmodule
