// Logisim project v5.circ as structural Verilog: 3 circuits, main circuit kolo1
module kolo1 (
  input  x1,
  input  x2,
  input  x3,
  input  x3_2
);

  wire n7_segment_display_driver_1_p5, n7_segment_display_driver_1_p6, n7_segment_display_driver_1_p7,
       n7_segment_display_driver_1_p8, n7_segment_display_driver_1_p10, n7_segment_display_driver_1_p11;

  // _7_segment_display_driver 7_segment_display_driver_1: pin names not known; wires that end beside it: x1, x2, x3, x3_2, n7_segment_display_driver_1_p5, n7_segment_display_driver_1_p6, n7_segment_display_driver_1_p7, n7_segment_display_driver_1_p8, n7_segment_display_driver_1_p7, n7_segment_display_driver_1_p10, n7_segment_display_driver_1_p11
  _7_Segment_Display u_7_segment_display_1 (
    .g(n7_segment_display_driver_1_p11), .f(n7_segment_display_driver_1_p8),
    .a(n7_segment_display_driver_1_p5), .b(n7_segment_display_driver_1_p6),
    .e(n7_segment_display_driver_1_p7), .d(n7_segment_display_driver_1_p10),
    .c(n7_segment_display_driver_1_p7));  // open: dp
endmodule

module kolo2 (
  input  D,
  input  C,
  input  B,
  input  A,
  output a_2,
  output b_2,
  output c_2,
  output d_2,
  output e,
  output f,
  output g
);

  wire and_1_out, and_2_out, and_3_out, and_4_out, and_5_out, and_6_out, and_7_out, and_8_out, and_9_out,
       and_10_out, and_11_out, and_12_out, and_13_out, and_14_out, and_15_out, and_16_out, and_17_out,
       and_18_out, and_19_out, and_20_out, and_21_out, and_22_out, and_23_out, and_24_out, and_25_out,
       and_26_out, and_27_out, and_28_out, and_29_out, and_30_out, and_31_out, and_32_out, and_33_out,
       and_34_out, and_35_out, and_36_out, and_37_out, and_38_out, and_39_out, and_40_out, and_41_out,
       and_42_out, and_43_out, and_44_out, and_45_out, and_46_out, and_47_out, not_1_out, not_2_out,
       not_3_out, not_4_out, not_5_out, not_6_out, not_7_out, not_8_out, not_9_out, not_10_out, not_11_out,
       not_12_out, not_13_out, not_14_out, not_15_out, not_16_out, not_17_out, not_18_out, not_19_out,
       not_20_out, not_21_out, not_22_out, not_23_out, not_24_out, not_25_out, not_26_out, not_27_out,
       not_28_out, not_29_out, not_30_out, not_31_out, not_32_out, not_33_out, not_34_out, not_35_out,
       not_36_out, not_37_out, not_38_out, not_39_out, not_40_out, not_41_out, not_42_out, not_43_out,
       not_44_out, or_1_out, or_2_out, or_3_out, or_4_out, or_5_out, or_6_out, or_7_out, or_8_out, or_9_out,
       or_10_out, or_12_out, or_13_out, or_14_out, or_15_out, or_16_out, or_17_out, or_18_out, or_20_out,
       or_21_out, or_22_out, or_23_out;

  not not_1 (not_1_out, C);
  not not_2 (not_2_out, A);
  not not_3 (not_3_out, D);
  not not_4 (not_4_out, D);
  and and_1 (and_1_out, D, not_5_out);
  not not_5 (not_5_out, C);
  not not_6 (not_6_out, B);
  not not_7 (not_7_out, D);
  not not_8 (not_8_out, C);
  not not_9 (not_9_out, D);
  and and_2 (and_2_out, not_9_out, not_10_out);
  not not_10 (not_10_out, B);
  not not_11 (not_11_out, A);
  not not_12 (not_12_out, D);
  not not_13 (not_13_out, B);
  not not_14 (not_14_out, D);
  and and_3 (and_3_out, not_14_out, not_15_out);
  not not_15 (not_15_out, B);
  not not_16 (not_16_out, D);
  and and_4 (and_4_out, not_16_out, A);
  not not_17 (not_17_out, B);
  not not_18 (not_18_out, D);
  not not_19 (not_19_out, C);
  not not_20 (not_20_out, D);
  and and_5 (and_5_out, not_20_out, not_21_out);
  not not_21 (not_21_out, C);
  not not_22 (not_22_out, A);
  not not_23 (not_23_out, C);
  and and_6 (and_6_out, not_23_out, B);
  not not_24 (not_24_out, B);
  not not_25 (not_25_out, B);
  not not_26 (not_26_out, C);
  and and_7 (and_7_out, not_26_out, not_27_out);
  not not_27 (not_27_out, A);
  and and_8 (and_8_out, B, not_28_out);
  not not_28 (not_28_out, A);
  and and_9 (and_9_out, D, B);
  and and_10 (and_10_out, D, C);
  not not_29 (not_29_out, B);
  not not_30 (not_30_out, A);
  not not_31 (not_31_out, D);
  and and_11 (and_11_out, not_31_out, C);
  not not_32 (not_32_out, B);
  not not_33 (not_33_out, C);
  and and_12 (and_12_out, not_33_out, B);
  and and_13 (and_13_out, B, not_34_out);
  not not_34 (not_34_out, A);
  not not_35 (not_35_out, D);
  and and_14 (and_14_out, not_35_out, C);
  not not_36 (not_36_out, B);
  not not_37 (not_37_out, C);
  and and_15 (and_15_out, not_1_out, not_2_out);
  and and_16 (and_16_out, not_3_out, B);
  and and_17 (and_17_out, not_4_out, C);
  and and_18 (and_18_out, C, B);
  and and_19 (and_19_out, and_1_out, not_6_out);
  not not_38 (not_38_out, A);
  and and_20 (and_20_out, not_7_out, not_8_out);
  and and_21 (and_21_out, and_2_out, not_11_out);
  not not_39 (not_39_out, C);
  not not_40 (not_40_out, A);
  and and_22 (and_22_out, not_12_out, B);
  and and_23 (and_23_out, D, not_13_out);
  or or_1 (or_1_out, and_3_out, and_4_out);
  and and_24 (and_24_out, not_17_out, A);
  and and_25 (and_25_out, not_18_out, C);
  and and_26 (and_26_out, D, not_19_out);
  and and_27 (and_27_out, and_5_out, not_22_out);
  and and_28 (and_28_out, and_6_out, A);
  and and_29 (and_29_out, C, not_24_out);
  and and_30 (and_30_out, C, B);
  not not_41 (not_41_out, A);
  and and_31 (and_31_out, D, not_25_out);
  not not_42 (not_42_out, A);
  or or_2 (or_2_out, and_7_out, and_8_out);
  or or_3 (or_3_out, and_9_out, and_10_out);
  and and_32 (and_32_out, not_29_out, not_30_out);
  and and_33 (and_33_out, and_11_out, not_32_out);
  not not_43 (not_43_out, A);
  not not_44 (not_44_out, C);
  or or_4 (or_4_out, and_12_out, and_13_out);
  and and_34 (and_34_out, and_14_out, not_36_out);
  and and_35 (and_35_out, D, not_37_out);
  and and_36 (and_36_out, D, A);
  or or_5 (or_5_out, and_15_out, and_16_out);
  and and_37 (and_37_out, and_17_out, A);
  or or_6 (or_6_out, and_18_out, and_19_out);
  and and_38 (and_38_out, D, not_38_out);
  or or_7 (or_7_out, and_20_out, and_21_out);
  and and_39 (and_39_out, not_39_out, not_40_out);
  and and_40 (and_40_out, and_22_out, A);
  and and_41 (and_41_out, and_23_out, A);
  or or_8 (or_8_out, or_1_out, and_24_out);
  or or_9 (or_9_out, and_25_out, and_26_out);
  or or_10 (or_10_out, and_27_out, and_28_out);
  and and_42 (and_42_out, and_29_out, A);
  and and_43 (and_43_out, and_30_out, not_41_out);
  and and_44 (and_44_out, and_31_out, not_42_out);
  or or_11 (e, or_2_out, or_3_out);
  or or_12 (or_12_out, and_32_out, and_33_out);
  and and_45 (and_45_out, C, not_43_out);
  and and_46 (and_46_out, D, not_44_out);
  and and_47 (and_47_out, D, B);
  or or_13 (or_13_out, or_4_out, and_34_out);
  or or_14 (or_14_out, and_35_out, and_36_out);
  or or_15 (or_15_out, or_5_out, and_37_out);
  or or_16 (or_16_out, or_6_out, and_38_out);
  or or_17 (or_17_out, or_7_out, and_39_out);
  or or_18 (or_18_out, and_40_out, and_41_out);
  or or_19 (c_2, or_8_out, or_9_out);
  or or_20 (or_20_out, or_10_out, and_42_out);
  or or_21 (or_21_out, and_43_out, and_44_out);
  or or_22 (or_22_out, or_12_out, and_45_out);
  or or_23 (or_23_out, and_46_out, and_47_out);
  or or_24 (g, or_13_out, or_14_out);
  or or_25 (a_2, or_15_out, or_16_out);
  or or_26 (b_2, or_17_out, or_18_out);
  or or_27 (d_2, or_20_out, or_21_out);
  or or_28 (f, or_22_out, or_23_out);
endmodule

module kolo3 (
  input  D,
  input  C,
  input  B,
  input  A,
  output a_2,
  output b_2,
  output c_2,
  output d_2,
  output e,
  output f,
  output g
);

  wire nand_1_out, nand_2_out, nand_3_out, nand_4_out, nand_5_out, nand_6_out, nand_7_out, nand_8_out,
       nand_9_out, nand_10_out, nand_11_out, nand_12_out, nand_13_out, nand_14_out, nand_15_out, nand_16_out,
       nand_17_out, nand_18_out, nand_19_out, nand_20_out, nand_21_out, nand_22_out, nand_23_out,
       nand_24_out, nand_25_out, nand_26_out, nand_27_out, nand_28_out, nand_29_out, nand_30_out,
       nand_31_out, nand_32_out, nand_33_out, nand_34_out, nand_35_out, nand_36_out, nand_37_out,
       nand_38_out, nand_39_out, nand_40_out, nand_41_out, nand_42_out, nand_43_out, nand_44_out,
       nand_45_out, nand_46_out, nand_47_out, nand_48_out, nand_49_out, nand_50_out, nand_51_out,
       nand_52_out, nand_53_out, nand_54_out, nand_55_out, nand_56_out, nand_57_out, nand_58_out,
       nand_59_out, nand_60_out, nand_61_out, nand_62_out, nand_63_out, nand_64_out, nand_65_out,
       nand_66_out, nand_67_out, nand_68_out, nand_69_out, nand_70_out, nand_71_out, nand_72_out,
       nand_73_out, nand_74_out, nand_75_out, nand_76_out, nand_77_out, nand_78_out, nand_79_out;

  nand nand_1 (nand_1_out, C, C);
  nand nand_2 (nand_2_out, A, A);
  nand nand_3 (nand_3_out, D, D);
  nand nand_4 (nand_4_out, D, D);
  nand nand_5 (nand_5_out, C, C);
  nand nand_6 (nand_6_out, B, B);
  nand nand_7 (nand_7_out, A, A);
  nand nand_8 (nand_8_out, D, D);
  nand nand_9 (nand_9_out, C, C);
  nand nand_10 (nand_10_out, D, D);
  nand nand_11 (nand_11_out, B, B);
  nand nand_12 (nand_12_out, A, A);
  nand nand_13 (nand_13_out, C, C);
  nand nand_14 (nand_14_out, A, A);
  nand nand_15 (nand_15_out, D, D);
  nand nand_16 (nand_16_out, B, B);
  nand nand_17 (nand_17_out, D, D);
  nand nand_18 (nand_18_out, B, B);
  nand nand_19 (nand_19_out, D, D);
  nand nand_20 (nand_20_out, B, B);
  nand nand_21 (nand_21_out, D, D);
  nand nand_22 (nand_22_out, C, C);
  nand nand_23 (nand_23_out, D, D);
  nand nand_24 (nand_24_out, C, C);
  nand nand_25 (nand_25_out, A, A);
  nand nand_26 (nand_26_out, C, C);
  nand nand_27 (nand_27_out, B, B);
  nand nand_28 (nand_28_out, A, A);
  nand nand_29 (nand_29_out, B, B);
  nand nand_30 (nand_30_out, A, A);
  nand nand_31 (nand_31_out, C, C);
  nand nand_32 (nand_32_out, A, A);
  nand nand_33 (nand_33_out, A, A);
  nand nand_34 (nand_34_out, B, B);
  nand nand_35 (nand_35_out, A, A);
  nand nand_36 (nand_36_out, D, D);
  nand nand_37 (nand_37_out, B, B);
  nand nand_38 (nand_38_out, A, A);
  nand nand_39 (nand_39_out, C, C);
  nand nand_40 (nand_40_out, C, C);
  nand nand_41 (nand_41_out, A, A);
  nand nand_42 (nand_42_out, D, D);
  nand nand_43 (nand_43_out, B, B);
  nand nand_44 (nand_44_out, C, C);
  nand nand_45 (nand_45_out, nand_1_out, nand_2_out);
  nand nand_46 (nand_46_out, nand_3_out, B);
  nand nand_47 (nand_47_out, nand_4_out, C, A);
  nand nand_48 (nand_48_out, C, B);
  nand nand_49 (nand_49_out, D, nand_5_out, nand_6_out);
  nand nand_50 (nand_50_out, D, nand_7_out);
  nand nand_51 (nand_51_out, nand_8_out, nand_9_out);
  nand nand_52 (nand_52_out, nand_10_out, nand_11_out, nand_12_out);
  nand nand_53 (nand_53_out, nand_13_out, nand_14_out);
  nand nand_54 (nand_54_out, nand_15_out, B, A);
  nand nand_55 (nand_55_out, D, nand_16_out, A);
  nand nand_56 (nand_56_out, nand_17_out, nand_18_out);
  nand nand_57 (nand_57_out, nand_19_out, A);
  nand nand_58 (nand_58_out, nand_20_out, A);
  nand nand_59 (nand_59_out, nand_21_out, C);
  nand nand_60 (nand_60_out, D, nand_22_out);
  nand nand_61 (nand_61_out, nand_23_out, nand_24_out, nand_25_out);
  nand nand_62 (nand_62_out, nand_26_out, B, A);
  nand nand_63 (nand_63_out, C, nand_27_out, A);
  nand nand_64 (nand_64_out, C, B, nand_28_out);
  nand nand_65 (nand_65_out, D, nand_29_out, nand_30_out);
  nand nand_66 (nand_66_out, nand_31_out, nand_32_out);
  nand nand_67 (nand_67_out, B, nand_33_out);
  nand nand_68 (nand_68_out, D, B);
  nand nand_69 (nand_69_out, D, C);
  nand nand_70 (nand_70_out, nand_34_out, nand_35_out);
  nand nand_71 (nand_71_out, nand_36_out, C, nand_37_out);
  nand nand_72 (nand_72_out, C, nand_38_out);
  nand nand_73 (nand_73_out, D, nand_39_out);
  nand nand_74 (nand_74_out, D, B);
  nand nand_75 (nand_75_out, nand_40_out, B);
  nand nand_76 (nand_76_out, B, nand_41_out);
  nand nand_77 (nand_77_out, nand_42_out, C, nand_43_out);
  nand nand_78 (nand_78_out, D, nand_44_out);
  nand nand_79 (nand_79_out, D, A);
  nand nand_80 (a_2, nand_45_out, nand_46_out, nand_47_out, nand_48_out, nand_49_out, nand_50_out);
  nand nand_81 (b_2, nand_51_out, nand_52_out, nand_53_out, nand_54_out, nand_55_out);
  nand nand_82 (c_2, nand_56_out, nand_57_out, nand_58_out, nand_59_out, nand_60_out);
  nand nand_83 (d_2, nand_61_out, nand_62_out, nand_63_out, nand_64_out, nand_65_out);
  nand nand_84 (e, nand_66_out, nand_67_out, nand_68_out, nand_69_out);
  nand nand_85 (f, nand_70_out, nand_71_out, nand_72_out, nand_73_out, nand_74_out);
  nand nand_86 (g, nand_75_out, nand_76_out, nand_77_out, nand_78_out, nand_79_out);
endmodule
