// Logisim project v6.circ as structural Verilog: 6 circuits, main circuit paljenje sijalice
module paljenje_sijalice (
  input  x1,
  input  x2,
  input  x3,
  output f
);

  or or_1 (f, x1, x2, x3);
endmodule

module gasenje_sijalice (
  input  x1,
  input  x2,
  input  x3,
  output f
);

  nand nand_1 (f, x1, x2, x3);
endmodule

module kolo1 (
  input  A,
  input  B,
  input  C,
  input  D,
  output f
);

  wire and_1_out, and_2_out, and_3_out, and_4_out, and_5_out, and_6_out, and_7_out, not_1_out, not_2_out,
       not_3_out, not_4_out, not_5_out, not_6_out, or_1_out, or_2_out;

  not not_1 (not_1_out, A);
  and and_1 (and_1_out, not_1_out, not_2_out);
  not not_2 (not_2_out, B);
  not not_3 (not_3_out, C);
  and and_2 (and_2_out, B, not_4_out);
  not not_4 (not_4_out, C);
  not not_5 (not_5_out, D);
  and and_3 (and_3_out, B, C);
  not not_6 (not_6_out, D);
  and and_4 (and_4_out, and_1_out, not_3_out);
  and and_5 (and_5_out, A, C);
  and and_6 (and_6_out, and_2_out, not_5_out);
  and and_7 (and_7_out, and_3_out, not_6_out);
  or or_1 (or_1_out, and_4_out, and_5_out);
  or or_2 (or_2_out, and_6_out, and_7_out);
  or or_3 (f, or_1_out, or_2_out);
endmodule

module kolo2 (
  input  A,
  input  B,
  input  C,
  input  D,
  output f
);

  wire and_1_out, and_2_out, and_3_out, and_4_out, and_5_out, and_6_out, and_7_out, not_1_out, not_2_out,
       not_3_out, not_4_out, not_5_out, or_1_out, or_2_out;

  not not_1 (not_1_out, C);
  not not_2 (not_2_out, B);
  not not_3 (not_3_out, C);
  not not_4 (not_4_out, A);
  and and_1 (and_1_out, not_4_out, B);
  and and_2 (and_2_out, A, B);
  and and_3 (and_3_out, C, not_5_out);
  not not_5 (not_5_out, D);
  and and_4 (and_4_out, not_1_out, D);
  and and_5 (and_5_out, not_2_out, not_3_out);
  and and_6 (and_6_out, and_1_out, D);
  and and_7 (and_7_out, and_2_out, and_3_out);
  or or_1 (or_1_out, and_4_out, and_5_out);
  or or_2 (or_2_out, and_6_out, and_7_out);
  or or_3 (f, or_1_out, or_2_out);
endmodule

module kolo3 (
  input  A,
  input  B,
  input  C,
  input  D,
  output f
);

  wire and_1_out, and_2_out, and_3_out, not_1_out, not_2_out, or_1_out;

  not not_1 (not_1_out, B);
  and and_1 (and_1_out, not_1_out, not_2_out);
  not not_2 (not_2_out, C);
  and and_2 (and_2_out, A, B);
  or or_1 (or_1_out, and_1_out, and_2_out);
  and and_3 (and_3_out, A, C);
  or or_2 (f, or_1_out, and_3_out);
endmodule

module kolo4 (
  input  A,
  input  B,
  input  C,
  input  D,
  output f
);

  wire not_1_out, not_2_out, not_3_out, or_1_out, or_2_out, or_3_out;

  not not_1 (not_1_out, C);
  not not_2 (not_2_out, A);
  or or_1 (or_1_out, not_2_out, C);
  not not_3 (not_3_out, D);
  or or_2 (or_2_out, B, not_1_out);
  or or_3 (or_3_out, or_1_out, not_3_out);
  and and_1 (f, or_2_out, or_3_out);
endmodule
