// Logisim project v8.circ as structural Verilog: 3 circuits, main circuit sef sale
module sef_sale (
  input  A,
  input  B,
  input  C,
  input  D,
  output f
);

  wire and_1_out, and_2_out, and_3_out;

  and and_1 (and_1_out, A, B);
  and and_2 (and_2_out, B, C, D);
  and and_3 (and_3_out, A, C, D);
  or or_1 (f, and_1_out, and_2_out, and_3_out);
endmodule

module sijalica_pali_gasi (
  input  x1,
  input  x2,
  input  x3,
  input  x4,
  output f
);

  wire and_1_out, and_2_out, and_3_out, and_4_out, and_5_out, and_6_out, not_1_out, not_2_out, not_3_out,
       not_4_out;

  not not_1 (not_1_out, x1);
  not not_2 (not_2_out, x2);
  not not_3 (not_3_out, x3);
  not not_4 (not_4_out, x4);
  and and_1 (and_1_out, not_1_out, not_2_out, not_3_out, x4);
  and and_2 (and_2_out, not_1_out, not_2_out, x3, not_4_out);
  and and_3 (and_3_out, not_4_out, not_3_out, x2);
  and and_4 (and_4_out, x1, not_3_out, not_4_out);
  and and_5 (and_5_out, x2, x3, x1);
  and and_6 (and_6_out, x4, x3, x1);
  or or_1 (f, and_6_out, and_1_out, and_2_out, and_3_out, and_4_out, and_5_out);
endmodule

module sijalica_pali_gasi1 (
  input  x1,
  input  x2,
  input  x3,
  input  x4,
  output f
);

  wire and_1_out, and_2_out, and_3_out, and_4_out, and_5_out, and_6_out, not_1_out, not_2_out, not_3_out,
       not_4_out, not_5_out, not_6_out, not_7_out, not_8_out, not_9_out, not_10_out;

  not not_1 (not_1_out, x1);
  not not_2 (not_2_out, x2);
  not not_3 (not_3_out, x3);
  not not_4 (not_4_out, x1);
  not not_5 (not_5_out, x2);
  not not_6 (not_6_out, x4);
  not not_7 (not_7_out, x3);
  not not_8 (not_8_out, x4);
  not not_9 (not_9_out, x3);
  not not_10 (not_10_out, x4);
  and and_1 (and_1_out, not_1_out, not_2_out, not_3_out, x4);
  and and_2 (and_2_out, not_4_out, not_5_out, x3, not_6_out);
  and and_3 (and_3_out, x2, not_7_out, not_8_out);
  and and_4 (and_4_out, x2, x3, x4);
  and and_5 (and_5_out, x1, not_9_out, not_10_out);
  and and_6 (and_6_out, x1, x3, x4);
  or or_1 (f, and_1_out, and_2_out, and_3_out, and_4_out, and_5_out, and_6_out);
endmodule
